// Digital circuit signal generator and character indexer.dig as structural Verilog
module signal_generator_and_character_indexer (
  input  pxl
);

  wire _7410_1_pin1, _7410_1_pin12, _7414_1_pin3, _7414_1_pin4, _7414_1_pin5, _7414_1_pin6, _7414_2_pin3,
       _7414_2_pin4, _7421_1_pin4, _7421_1_pin5, _7421_1_pin9, _7421_1_pin10, _7421_1_pin12, _7421_1_pin13,
       _7421_2_pin8, _74133_1_pin1, _74133_1_pin2, _74133_1_pin3, _74133_1_pin4, _74133_1_pin9,
       _74133_1_pin10, _74133_1_pin11, _74133_1_pin12, _74133_1_pin13, _74133_1_pin14, _74133_1_pin15,
       _74161_1_pin1, _74161_1_pin11, _74161_1_pin12, _74161_1_pin13, _74161_1_pin14, _74161_2_pin11,
       _74161_2_pin12, _74161_2_pin13, _74161_2_pin14, _74161_2_pin15, _74161_3_pin14, _74161_4_pin13,
       _74161_4_pin15, _74161_5_pin11, _74161_5_pin12, _74161_5_pin13, _74161_5_pin14, _74161_5_pin15,
       _74161_6_pin14;

  _74161 _74161_1 (
    .pin1(_74161_1_pin1), .pin2(pxl), .pin3(1'b0), .pin4(1'b0), .pin5(1'b0), .pin6(1'b0), .pin7(1'b1),
    .pin8(1'b0), .pin9(1'b1), .pin10(1'b1), .pin11(_74161_1_pin11), .pin12(_74161_1_pin12),
    .pin13(_74161_1_pin13), .pin14(_74161_1_pin14), .pin16(1'b1));  // open: pin15
  _7414 _7414_1 (
    .pin1(_74161_1_pin11), .pin2(_74161_1_pin1), .pin3(_7414_1_pin3), .pin4(_7414_1_pin4),
    .pin5(_7414_1_pin5), .pin6(_7414_1_pin6), .pin7(1'b0), .pin9(1'b0), .pin11(1'b0), .pin13(1'b0),
    .pin14(1'b1));  // open: pin8, pin10, pin12
  _74161 _74161_2 (
    .pin1(_7414_1_pin6), .pin2(_74161_1_pin11), .pin3(1'b0), .pin4(1'b0), .pin5(1'b0), .pin6(1'b0),
    .pin7(1'b1), .pin8(1'b0), .pin9(1'b1), .pin10(1'b1), .pin11(_74161_2_pin11), .pin12(_74161_2_pin12),
    .pin13(_74161_2_pin13), .pin14(_74161_2_pin14), .pin15(_74161_2_pin15), .pin16(1'b1));
  _7421 _7421_1 (
    .pin1(_74161_2_pin12), .pin2(1'b1), .pin4(_7421_1_pin4), .pin5(_7421_1_pin5), .pin6(_7414_1_pin5),
    .pin7(1'b0), .pin8(_7414_1_pin3), .pin9(_7421_1_pin9), .pin10(_7421_1_pin10), .pin12(_7421_1_pin12),
    .pin13(_7421_1_pin13), .pin14(1'b1));  // open: pin3, pin11
  _74161 _74161_3 (
    .pin1(_7414_1_pin6), .pin2(_74161_1_pin11), .pin3(1'b0), .pin4(1'b0), .pin5(1'b0), .pin6(1'b0),
    .pin7(1'b1), .pin8(1'b0), .pin9(1'b1), .pin10(_74161_2_pin15), .pin12(_7421_1_pin4),
    .pin13(_7421_1_pin5), .pin14(_74161_3_pin14), .pin16(1'b1));  // open: pin11, pin15
  _74161 _74161_4 (
    .pin1(_7414_1_pin4), .pin2(_7414_1_pin6), .pin3(1'b0), .pin4(1'b0), .pin5(1'b0), .pin6(1'b0),
    .pin7(1'b1), .pin8(1'b0), .pin9(1'b1), .pin10(1'b1), .pin11(_7421_1_pin12), .pin12(_7421_1_pin10),
    .pin13(_74161_4_pin13), .pin14(_7421_1_pin9), .pin15(_74161_4_pin15), .pin16(1'b1));
  _74161 _74161_5 (
    .pin1(_7414_1_pin4), .pin2(_7414_1_pin6), .pin3(1'b0), .pin4(1'b0), .pin5(1'b0), .pin6(1'b0),
    .pin7(1'b1), .pin8(1'b0), .pin9(1'b1), .pin10(_74161_4_pin15), .pin11(_74161_5_pin11),
    .pin12(_74161_5_pin12), .pin13(_74161_5_pin13), .pin14(_74161_5_pin14), .pin15(_74161_5_pin15),
    .pin16(1'b1));
  _74161 _74161_6 (
    .pin1(_7414_1_pin4), .pin2(_7414_1_pin6), .pin3(1'b0), .pin4(1'b0), .pin5(1'b0), .pin6(1'b0),
    .pin7(1'b1), .pin8(1'b0), .pin9(1'b1), .pin10(_74161_5_pin15), .pin13(_7421_1_pin13),
    .pin14(_74161_6_pin14), .pin16(1'b1));  // open: pin11, pin12, pin15
  _7410 _7410_1 (
    .pin1(_7410_1_pin1), .pin2(_7421_1_pin4), .pin3(1'b0), .pin4(1'b0), .pin5(1'b0), .pin7(1'b0),
    .pin9(1'b1), .pin10(1'b1), .pin11(1'b1), .pin12(_7410_1_pin12), .pin13(_74161_3_pin14), .pin14(1'b1));  // open: pin6, pin8
  _7414 _7414_2 (
    .pin1(_7421_1_pin5), .pin2(_7410_1_pin1), .pin3(_7414_2_pin3), .pin4(_7414_2_pin4), .pin5(1'b0),
    .pin7(1'b0), .pin9(1'b0), .pin11(1'b0), .pin13(1'b0), .pin14(1'b1));  // open: pin6, pin8, pin10, pin12
  _74133 _74133_1 (
    .pin1(_74133_1_pin1), .pin2(_74133_1_pin2), .pin3(_74133_1_pin3), .pin4(_74133_1_pin4), .pin5(1'b1),
    .pin6(1'b1), .pin7(1'b1), .pin8(1'b0), .pin9(_74133_1_pin9), .pin10(_74133_1_pin10),
    .pin11(_74133_1_pin11), .pin12(_74133_1_pin12), .pin13(_74133_1_pin13), .pin14(_74133_1_pin14),
    .pin15(_74133_1_pin15), .pin16(1'b1));
  _7421 _7421_2 (
    .pin1(_74161_5_pin13), .pin2(_74161_5_pin12), .pin4(_74161_5_pin11), .pin5(_74161_6_pin14),
    .pin6(_7414_2_pin3), .pin7(1'b0), .pin8(_7421_2_pin8), .pin9(_7414_2_pin3), .pin10(1'b1), .pin12(1'b1),
    .pin13(_74133_1_pin9), .pin14(1'b1));  // open: pin3, pin11
  _74154 _74154_1 (
    .pin1(_74133_1_pin4), .pin2(_74133_1_pin3), .pin3(_74133_1_pin2), .pin4(_74133_1_pin1),
    .pin5(_74133_1_pin15), .pin6(_74133_1_pin14), .pin7(_74133_1_pin13), .pin8(_74133_1_pin12),
    .pin9(_74133_1_pin11), .pin10(_74133_1_pin10), .pin12(1'b0), .pin18(1'b0), .pin19(1'b0),
    .pin20(_7421_1_pin12), .pin21(_7421_1_pin10), .pin22(_74161_4_pin13), .pin23(_7421_1_pin9), .pin24(1'b1));  // open: pin11, pin13, pin14, pin15, pin16, pin17
  // Probe hvis on _7410_1_pin12
  // Probe vVis on _7414_2_pin4

  // Notes on the sheet:
  //   pxl: Hz: 5000
  //   Horizontal character counter
  //   Pixel clock divider
  //   Line counter
  //   Character pixel horizontal (0-7)
  //   Character index horizontal (0-99)
  //   Current line vertical (0-524)
  //   High when in hvis (chars 0-79)
  //   High when in vVis (lines 0-479)
  //   High when in vFrontPorch (lines 480-489)
endmodule
